// Logisim project d_flip_flop.circ as structural Verilog
module d_flip_flop_compare (
  input  D,
  input  CLK,
  output Q_gate,
  output Q_n_gate,
  output Q_vhdl,
  output Q_n_vhdl
);

  wire nand_1_out, nand_2_out, nand_3_out, nand_4_out, nand_5_out, nand_6_out, nand_7_out, nand_8_out,
       not_1_out;

  not not_1 (not_1_out, CLK);
  nand nand_1 (nand_1_out, D, D);
  d_flip_flop d_flip_flop_1 (.d(D), .clk(CLK), .q(Q_vhdl), .q_n(Q_n_vhdl));
  nand nand_2 (nand_2_out, D, not_1_out);
  nand nand_3 (nand_3_out, nand_1_out, not_1_out);
  nand nand_4 (nand_4_out, nand_2_out, nand_5_out);
  nand nand_5 (nand_5_out, nand_4_out, nand_3_out);
  nand nand_6 (nand_6_out, nand_4_out, nand_4_out);
  nand nand_7 (nand_7_out, nand_4_out, CLK);
  nand nand_8 (nand_8_out, nand_6_out, CLK);
  nand nand_9 (Q_gate, nand_7_out, Q_n_gate);
  nand nand_10 (Q_n_gate, Q_gate, nand_8_out);

  // Notes on the sheet:
  //   Gate-level implementation
  //   VHDL implementation
  //   Master D latch
  //   Slave D latch
endmodule

// VHDL entity d_flip_flop, as the project stores it:
library ieee;
use ieee.std_logic_1164.all;

entity d_flip_flop is
    port (
        d   : in  std_logic;
        clk : in  std_logic;
        q   : out std_logic;
        q_n : out std_logic
    );
end entity d_flip_flop;

architecture rtl of d_flip_flop is
    signal stored : std_logic;
begin
    capture : process(clk)
    begin
        if rising_edge(clk) then
            stored <= d;
        end if;
    end process;

    q   <= stored;
    q_n <= not stored;
end architecture rtl;
