// Logisim project d_flip_flop_async.circ as structural Verilog
module d_flip_flop_async_compare (
  input  SET,
  input  CLR,
  input  CLK,
  input  D,
  output Q_gate,
  output Q_n_gate,
  output Q_vhdl,
  output Q_n_vhdl
);

  wire and_1_out, and_2_out, and_3_out, and_4_out, nand_1_out, nand_2_out, nand_3_out, nand_4_out,
       nand_5_out, nand_6_out, nand_7_out, nor_1_out, not_1_out, not_2_out, not_3_out, not_4_out;

  not not_1 (not_1_out, CLR);
  not not_2 (not_2_out, CLK);
  not not_3 (not_3_out, D);
  not not_4 (not_4_out, nand_6_out);
  d_flip_flop_async d_flip_flop_async_1 (.d(D), .clk(CLK), .set(SET), .clr(CLR), .q(Q_vhdl), .q_n(Q_n_vhdl));
  nand nand_1 (nand_1_out, SET, not_1_out);
  nor nor_1 (nor_1_out, SET, CLR);
  nand nand_2 (nand_2_out, D, not_2_out, nor_1_out);
  nand nand_3 (nand_3_out, not_3_out, not_2_out, nor_1_out);
  nand nand_4 (nand_4_out, nand_6_out, CLK, nor_1_out);
  nand nand_5 (nand_5_out, not_4_out, CLK, nor_1_out);
  and and_1 (and_1_out, nand_2_out, nand_1_out);
  and and_2 (and_2_out, nand_3_out, not_1_out);
  and and_3 (and_3_out, nand_4_out, nand_1_out);
  and and_4 (and_4_out, nand_5_out, not_1_out);
  nand nand_6 (nand_6_out, and_1_out, nand_7_out);
  nand nand_7 (nand_7_out, nand_6_out, and_2_out);
  nand nand_8 (Q_gate, and_3_out, Q_n_gate);
  nand nand_9 (Q_n_gate, Q_gate, and_4_out);

  // Notes on the sheet:
  //   CLR: initial=0x1
  //   Gate-level implementation
  //   VHDL implementation
  //   Clear priority and clock inversion
  //   Master latch
  //   Slave latch
endmodule

// VHDL entity d_flip_flop_async, as the project stores it:
library ieee;
use ieee.std_logic_1164.all;

entity d_flip_flop_async is
    port (
        d    : in  std_logic;
        clk  : in  std_logic;
        set  : in  std_logic;
        clr  : in  std_logic;
        q    : out std_logic;
        q_n  : out std_logic
    );
end entity d_flip_flop_async;

architecture rtl of d_flip_flop_async is
    signal stored : std_logic;
begin
    update_state : process(clk, set, clr)
    begin
        if clr = '1' then
            stored <= '0';
        elsif set = '1' then
            stored <= '1';
        elsif rising_edge(clk) then
            stored <= d;
        end if;
    end process;

    q   <= stored;
    q_n <= not stored;
end architecture rtl;
