// Logisim project d_latch.circ as structural Verilog
module d_latch_compare (
  input  D,
  input  EN,
  output Q_gate,
  output Q_n_gate,
  output Q_vhdl,
  output Q_n_vhdl
);

  wire nand_1_out, nand_2_out, nand_3_out;

  nand nand_1 (nand_1_out, D, D);
  d_latch d_latch_1 (.d(D), .en(EN), .q(Q_vhdl), .q_n(Q_n_vhdl));
  nand nand_2 (nand_2_out, D, EN);
  nand nand_3 (nand_3_out, nand_1_out, EN);
  nand nand_4 (Q_gate, nand_2_out, Q_n_gate);
  nand nand_5 (Q_n_gate, Q_gate, nand_3_out);

  // Notes on the sheet:
  //   EN: initial=0x1
  //   Gate-level implementation
  //   VHDL implementation
endmodule

// VHDL entity d_latch, as the project stores it:
library ieee;
use ieee.std_logic_1164.all;

entity d_latch is
    port (
        d   : in  std_logic;
        en  : in  std_logic;
        q   : out std_logic;
        q_n : out std_logic
    );
end entity d_latch;

architecture rtl of d_latch is
    signal stored : std_logic;
begin
    latch_d : process(d, en)
    begin
        if en = '1' then
            stored <= d;
        end if;
    end process;

    q   <= stored;
    q_n <= not stored;
end architecture rtl;
