// Logisim project jk_flip_flop.circ as structural Verilog
module jk_flip_flop_compare (
  input  CLK,
  input  J,
  input  K,
  output Q_gate,
  output Q_n_gate,
  output Q_vhdl,
  output Q_n_vhdl
);

  wire D_JK, K_N, nand_1_out, nand_2_out, nand_3_out, nand_4_out, nand_7_out, nand_8_out, nand_10_out,
       nand_12_out, nand_13_out, NJ, NK;

  nand nand_1 (nand_1_out, CLK, CLK);
  nand nand_2 (nand_2_out, D_JK, D_JK);
  jk_flip_flop jk_flip_flop_1 (.j(J), .k(K), .clk(CLK), .q(Q_vhdl), .q_n(Q_n_vhdl));
  nand nand_3 (nand_3_out, D_JK, nand_1_out);
  nand nand_4 (nand_4_out, nand_2_out, nand_1_out);
  nand nand_5 (NJ, J, Q_n_gate);
  nand nand_6 (K_N, K, K);
  nand nand_7 (nand_7_out, nand_3_out, nand_8_out);
  nand nand_8 (nand_8_out, nand_7_out, nand_4_out);
  nand nand_9 (NK, K_N, Q_gate);
  nand nand_10 (nand_10_out, nand_7_out, nand_7_out);
  nand nand_11 (D_JK, NJ, NK);
  nand nand_12 (nand_12_out, nand_7_out, CLK);
  nand nand_13 (nand_13_out, nand_10_out, CLK);
  nand nand_14 (Q_gate, nand_12_out, Q_n_gate);
  nand nand_15 (Q_n_gate, Q_gate, nand_13_out);

  // Other names for the same wires on the sheet: FB_Q = Q_gate; FB_QN = Q_n_gate

  // Notes on the sheet:
  //   K: initial=0x1
  //   Gate-level implementation
  //   VHDL implementation
  //   Master D latch
  //   JK next-state logic
  //   Slave D latch
endmodule

// VHDL entity jk_flip_flop, as the project stores it:
library ieee;
use ieee.std_logic_1164.all;

entity jk_flip_flop is
    port (
        j    : in  std_logic;
        k    : in  std_logic;
        clk  : in  std_logic;
        q    : out std_logic;
        q_n  : out std_logic
    );
end entity jk_flip_flop;

architecture rtl of jk_flip_flop is
    signal stored : std_logic;
begin
    update_state : process(clk)
    begin
        if rising_edge(clk) then
            case std_logic_vector'(j & k) is
                when "00" => null;
                when "01" => stored <= '0';
                when "10" => stored <= '1';
                when "11" => stored <= not stored;
                when others => stored <= 'X';
            end case;
        end if;
    end process;

    q   <= stored;
    q_n <= not stored;
end architecture rtl;
