// Logisim project rs_latch.circ as structural Verilog
module rs_latch_compare (
  input  R,
  input  S,
  output Q_gate,
  output Q_n_gate,
  output Q_vhdl,
  output Q_n_vhdl
);

  rs_latch rs_latch_1 (.s(S), .r(R), .q(Q_vhdl), .q_n(Q_n_vhdl));
  nor nor_1 (Q_gate, R, Q_n_gate);
  nor nor_2 (Q_n_gate, Q_gate, S);

  // Notes on the sheet:
  //   R: initial=0x1
  //   Gate-level implementation
  //   VHDL implementation
endmodule

// VHDL entity rs_latch, as the project stores it:
library ieee;
use ieee.std_logic_1164.all;

entity rs_latch is
    port (
        s   : in  std_logic;
        r   : in  std_logic;
        q   : out std_logic;
        q_n : out std_logic
    );
end entity rs_latch;

architecture nor_gates of rs_latch is
    signal q_feedback   : std_logic;
    signal q_n_feedback : std_logic;
begin
    q_feedback   <= r nor q_n_feedback;
    q_n_feedback <= s nor q_feedback;

    q   <= q_feedback;
    q_n <= q_n_feedback;
end architecture nor_gates;
